# Fritzing sketch prototype (saved by Fritzing 0.9.3b)
breadboards: 1

parts:
  Mod1 = Raspberry Pi Pico W
  Q1 = MOSFET-NCHANNEL [package=to220v]
  Q2 = MOSFET-NCHANNEL [package=to220v]
  F1 = Fan - Ventilador [package=THT]
  F2 = Fan - Ventilador [package=THT]
  R2 = Resistor [tolerance=±5% resistance=10k package=THT]
  R3 = Temperature Sensor (Thermistor) [thermistor_type=NTC package=THT]
  R4 = Temperature Sensor (Thermistor) [thermistor_type=NTC package=THT]
  R1 = Resistor [tolerance=±5% resistance=10k package=THT]

nets:
  N1: Mod1.pin_3, Mod1.pin_8, Mod1.pin_13, Mod1.pin_18, Mod1.pin_23, Mod1.pin_28, Mod1.pin_33, Mod1.pin_38, Mod1.pin_42, Q1.S, Q2.S, R3.pin_1, R4.pin_1
  N2: Mod1.pin_19, Q2.G
  N3: Mod1.pin_20, Q1.G
  N4: Mod1.pin_31, R1.Pin_1
  N5: Mod1.pin_32, R2.Pin_1
  N6: Q1.D, F1.GND
  N7: Q2.D, F2.GND
  5V: F1.5V, F2.5V

custom parts:
  Raspberry Pi Pico W: Raspberry Pi Pico W. Based around the RP2040 microcontroller the Pico W is a low cost microcontroller device bringing Raspberry Pi quality, cost, and easy of use to the microcontroller space. The areas marked KEEPOUT in pcb silkscreen should not have traces running through them to avoid shorts on a soldered in module!
  Fan - Ventilador: Ventilador de 2 pines, se encuentra comunmente en computadoras de escritorio
